// Logisim project control-logic.circ as structural Verilog: 1 circuit, main circuit control_logic
module control_logic (
  input  [31:0] Instruction,
  input  BrEq,
  input  BrLt,
  output PCSel,
  output RegWEn,
  output [2:0] ImmSel,
  output BrUn,
  output ASel,
  output BSel,
  output [3:0] ALUSel,
  output MemWEn,
  output [1:0] WBSel
);

  wire and_17_out, and_18_out, and_19_out, and_20_out, not_1_out, not_2_out, or_1_out, or_2_out, ROM0, ROM1,
       ROM2, ROM3, ROM4, ROM5, ROM6, ROM7, ROM8, ROM9, ROM10, ROM11, ROM12, ROM13, ROM14, ROM15, ROM16,
       ROM17, ROM18, ROM19, ROM20, ROM21, ROM22, ROM23, ROM24, ROM25, ROM26, ROM27, ROM28, ROM29, ROM30,
       ROM31, ROM32, ROM33, ROM34, ROM35;
  wire [5:0] ROMInput;
  wire [15:14] rom_1_data;
  wire [31:0] and_1_out, and_2_out, and_3_out, and_4_out, and_5_out, and_6_out, and_7_out, and_8_out,
       and_9_out, and_10_out, and_11_out, and_12_out, and_13_out, and_14_out, and_15_out, and_16_out,
       and_21_out, and_22_out, and_23_out, and_24_out, and_25_out, and_26_out, and_27_out, and_28_out,
       and_29_out, and_30_out, and_31_out, and_32_out, and_33_out, and_34_out, and_35_out, and_36_out,
       and_37_out, and_38_out, and_39_out, and_40_out;

  Priority_Encoder #(.select_enc(6)) priority_encoder_1 (
    .in0(ROM0), .in1(ROM1), .in2(ROM2), .in3(ROM3), .in4(ROM4), .in5(ROM5), .in6(ROM6), .in7(ROM7),
    .in8(ROM8), .in9(ROM9), .in10(ROM10), .in11(ROM11), .in12(ROM12), .in13(ROM13), .in14(ROM14),
    .in15(ROM15), .in16(ROM16), .in17(ROM17), .in18(ROM18), .in19(ROM19), .in20(ROM20), .in21(ROM21),
    .in22(ROM22), .in23(ROM23), .in24(ROM24), .in25(ROM25), .in26(ROM26), .in27(ROM27), .in28(ROM28),
    .in29(ROM29), .in30(ROM30), .in31(ROM31), .in32(ROM32), .in33(ROM33), .in34(ROM34), .in35(ROM35),
    .out(ROMInput));  // open: in36, in37, in38, in39, in40, in41, in42, in43, in44, in45, in46, in47, in48, in49, in50, in51, in52, in53, in54, in55, in56, in57, in58, in59, in60, in61, in62, in63, gs, en_out, en_in
  ROM #(.addrWidth(6), .dataWidth(16)) rom_1 (
    .addr(ROMInput), .data({rom_1_data, WBSel, MemWEn, ALUSel, BSel, ASel, BrUn, ImmSel, RegWEn}));
  assign and_1_out = 32'hfe00707f & Instruction;  // AND_Gate and_1, 32 bits wide
  assign and_2_out = 32'hfe00707f & Instruction;  // AND_Gate and_2, 32 bits wide
  assign and_3_out = 32'hfe00707f & Instruction;  // AND_Gate and_3, 32 bits wide
  assign and_4_out = 32'hfe00707f & Instruction;  // AND_Gate and_4, 32 bits wide
  assign and_5_out = 32'hfe00707f & Instruction;  // AND_Gate and_5, 32 bits wide
  assign and_6_out = 32'hfe00707f & Instruction;  // AND_Gate and_6, 32 bits wide
  assign and_7_out = 32'hfe00707f & Instruction;  // AND_Gate and_7, 32 bits wide
  assign and_8_out = 32'hfe00707f & Instruction;  // AND_Gate and_8, 32 bits wide
  Comparator #(.width(32)) comparator_1 (.a(32'h33), .b(and_1_out), .eq(ROM0));  // open: gt, lt
  Comparator #(.width(32)) comparator_2 (.a(32'h2000033), .b(and_2_out), .eq(ROM1));  // open: gt, lt
  Comparator #(.width(32)) comparator_3 (.a(32'h40000033), .b(and_3_out), .eq(ROM2));  // open: gt, lt
  Comparator #(.width(32)) comparator_4 (.a(32'h1033), .b(and_4_out), .eq(ROM3));  // open: gt, lt
  Comparator #(.width(32)) comparator_5 (.a(32'h2001033), .b(and_5_out), .eq(ROM4));  // open: gt, lt
  Comparator #(.width(32)) comparator_6 (.a(32'h2003033), .b(and_6_out), .eq(ROM5));  // open: gt, lt
  Comparator #(.width(32)) comparator_7 (.a(32'h2033), .b(and_7_out), .eq(ROM6));  // open: gt, lt
  Comparator #(.width(32)) comparator_8 (.a(32'h4033), .b(and_8_out), .eq(ROM7));  // open: gt, lt
  Comparator #(.width(32)) comparator_9 (.a(32'h5033), .b(and_9_out), .eq(ROM8));  // open: gt, lt
  assign and_9_out = 32'hfe00707f & Instruction;  // AND_Gate and_9, 32 bits wide
  Comparator #(.width(32)) comparator_10 (.a(32'h40005033), .b(and_10_out), .eq(ROM9));  // open: gt, lt
  assign and_10_out = 32'hfe00707f & Instruction;  // AND_Gate and_10, 32 bits wide
  Comparator #(.width(32)) comparator_11 (.a(32'h6033), .b(and_11_out), .eq(ROM10));  // open: gt, lt
  assign and_11_out = 32'hfe00707f & Instruction;  // AND_Gate and_11, 32 bits wide
  Comparator #(.width(32)) comparator_12 (.a(32'h7033), .b(and_12_out), .eq(ROM11));  // open: gt, lt
  assign and_12_out = 32'hfe00707f & Instruction;  // AND_Gate and_12, 32 bits wide
  Comparator #(.width(32)) comparator_13 (.a(32'h3), .b(and_13_out), .eq(ROM12));  // open: gt, lt
  assign and_13_out = 32'h707f & Instruction;  // AND_Gate and_13, 32 bits wide
  Comparator #(.width(32)) comparator_14 (.a(32'h1003), .b(and_14_out), .eq(ROM13));  // open: gt, lt
  assign and_14_out = 32'h707f & Instruction;  // AND_Gate and_14, 32 bits wide
  Comparator #(.width(32)) comparator_15 (.a(32'h2003), .b(and_15_out), .eq(ROM14));  // open: gt, lt
  assign and_15_out = 32'h707f & Instruction;  // AND_Gate and_15, 32 bits wide
  Comparator #(.width(32)) comparator_16 (.a(32'h13), .b(and_16_out), .eq(ROM15));  // open: gt, lt
  assign and_16_out = 32'h707f & Instruction;  // AND_Gate and_16, 32 bits wide
  not not_1 (not_1_out, BrEq);
  not not_2 (not_2_out, BrLt);
  and and_17 (and_17_out, ROM26, BrEq);
  and and_18 (and_18_out, ROM27, not_1_out);
  or or_1 (or_1_out, ROM28, ROM30);
  or or_2 (or_2_out, ROM29, ROM31);
  and and_19 (and_19_out, or_1_out, BrLt);
  and and_20 (and_20_out, or_2_out, not_2_out);
  assign and_21_out = 32'hfe00707f & Instruction;  // AND_Gate and_21, 32 bits wide
  assign and_22_out = 32'h707f & Instruction;  // AND_Gate and_22, 32 bits wide
  assign and_23_out = 32'h707f & Instruction;  // AND_Gate and_23, 32 bits wide
  assign and_24_out = 32'hfe00707f & Instruction;  // AND_Gate and_24, 32 bits wide
  assign and_25_out = 32'hfe00707f & Instruction;  // AND_Gate and_25, 32 bits wide
  assign and_26_out = 32'h707f & Instruction;  // AND_Gate and_26, 32 bits wide
  assign and_27_out = 32'h707f & Instruction;  // AND_Gate and_27, 32 bits wide
  assign and_28_out = 32'h707f & Instruction;  // AND_Gate and_28, 32 bits wide
  Comparator #(.width(32)) comparator_17 (.a(32'h1013), .b(and_21_out), .eq(ROM16));  // open: gt, lt
  Comparator #(.width(32)) comparator_18 (.a(32'h2013), .b(and_22_out), .eq(ROM17));  // open: gt, lt
  Comparator #(.width(32)) comparator_19 (.a(32'h4013), .b(and_23_out), .eq(ROM18));  // open: gt, lt
  Comparator #(.width(32)) comparator_20 (.a(32'h5013), .b(and_24_out), .eq(ROM19));  // open: gt, lt
  Comparator #(.width(32)) comparator_21 (.a(32'h40005013), .b(and_25_out), .eq(ROM20));  // open: gt, lt
  Comparator #(.width(32)) comparator_22 (.a(32'h6013), .b(and_26_out), .eq(ROM21));  // open: gt, lt
  Comparator #(.width(32)) comparator_23 (.a(32'h7013), .b(and_27_out), .eq(ROM22));  // open: gt, lt
  Comparator #(.width(32)) comparator_24 (.a(32'h23), .b(and_28_out), .eq(ROM23));  // open: gt, lt
  or or_3 (PCSel, and_17_out, and_18_out, and_19_out, and_20_out, ROM34, ROM35);
  assign and_29_out = 32'h707f & Instruction;  // AND_Gate and_29, 32 bits wide
  assign and_30_out = 32'h707f & Instruction;  // AND_Gate and_30, 32 bits wide
  assign and_31_out = 32'h707f & Instruction;  // AND_Gate and_31, 32 bits wide
  assign and_32_out = 32'h707f & Instruction;  // AND_Gate and_32, 32 bits wide
  assign and_33_out = 32'h707f & Instruction;  // AND_Gate and_33, 32 bits wide
  assign and_34_out = 32'h707f & Instruction;  // AND_Gate and_34, 32 bits wide
  assign and_35_out = 32'h707f & Instruction;  // AND_Gate and_35, 32 bits wide
  assign and_36_out = 32'h707f & Instruction;  // AND_Gate and_36, 32 bits wide
  Comparator #(.width(32)) comparator_25 (.a(32'h1023), .b(and_29_out), .eq(ROM24));  // open: gt, lt
  Comparator #(.width(32)) comparator_26 (.a(32'h2023), .b(and_30_out), .eq(ROM25));  // open: gt, lt
  Comparator #(.width(32)) comparator_27 (.a(32'h63), .b(and_31_out), .eq(ROM26));  // open: gt, lt
  Comparator #(.width(32)) comparator_28 (.a(32'h1063), .b(and_32_out), .eq(ROM27));  // open: gt, lt
  Comparator #(.width(32)) comparator_29 (.a(32'h4063), .b(and_33_out), .eq(ROM28));  // open: gt, lt
  Comparator #(.width(32)) comparator_30 (.a(32'h5063), .b(and_34_out), .eq(ROM29));  // open: gt, lt
  Comparator #(.width(32)) comparator_31 (.a(32'h6063), .b(and_35_out), .eq(ROM30));  // open: gt, lt
  Comparator #(.width(32)) comparator_32 (.a(32'h7063), .b(and_36_out), .eq(ROM31));  // open: gt, lt
  assign and_37_out = 32'h7f & Instruction;  // AND_Gate and_37, 32 bits wide
  assign and_38_out = 32'h7f & Instruction;  // AND_Gate and_38, 32 bits wide
  assign and_39_out = 32'h7f & Instruction;  // AND_Gate and_39, 32 bits wide
  assign and_40_out = 32'h707f & Instruction;  // AND_Gate and_40, 32 bits wide
  Comparator #(.width(32)) comparator_33 (.a(32'h17), .b(and_37_out), .eq(ROM32));  // open: gt, lt
  Comparator #(.width(32)) comparator_34 (.a(32'h37), .b(and_38_out), .eq(ROM33));  // open: gt, lt
  Comparator #(.width(32)) comparator_35 (.a(32'h6f), .b(and_39_out), .eq(ROM34));  // open: gt, lt
  Comparator #(.width(32)) comparator_36 (.a(32'h67), .b(and_40_out), .eq(ROM35));  // open: gt, lt

  // Notes on the sheet:
  //   INPUTS to your circuit
  //   contents of rom_1 (hex, n*v repeats v):
  //   1061 1461 1661 10e1 14e1 15e1 1161 1261 12e1 16e1 1361 13e1 21 21 21 1021 10a1 1121 1221 12a1 16a1
  //   1321 13a1 1822 1822 1822 4*1004 1014 1014 1007 1787 2009 2021
  //   ROM FOR CONTROL LOGIC
  //   DON'T CHANGE THE LOCATIONS OF THE INPUTS AND OUTPUTS!
  //   This is only if you choose to do the ROM option
  //   OUTPUT from your circuit
  //   Reminder: If using ROM, use combinational logic for PCSel
endmodule
