// Logisim project cpu.circ as structural Verilog: 1 circuit, main circuit cpu
module cpu (
  input  clk,
  input  [31:0] Instruction,
  input  [31:0] MemReadData,
  output [31:0] MemAddress,
  output [31:0] ProgramCounter,
  output [31:0] ra,
  output [31:0] sp,
  output [31:0] t0,
  output [31:0] t1,
  output [31:0] t2,
  output [31:0] s0,
  output [31:0] s1,
  output [31:0] a0,
  output [3:0] MemWriteMask,
  output [31:0] MemWriteData
);

  wire ASel, BrEq, BrLt, BrUn, BSel, MemWEn, PCSel, RegWEn;
  wire [1:0] WBSEl;
  wire [2:0] ImmSel;
  wire [3:0] ALUSel;
  wire [31:0] adder_2_out, Immediate, Instruction_t, MemDataToReg, multiplexer_1_out, multiplexer_2_out,
       multiplexer_4_out, multiplexer_5_out, PCInc, RegReadData1, RegReadData2, RegWriteData;

  Register #(.width(32)) PC (.D(multiplexer_1_out), .clk(clk), .Q(ProgramCounter));  // open: en, clr
  Multiplexer #(.width(32)) multiplexer_1 (.in0(PCInc), .in1(MemAddress), .out(multiplexer_1_out), .sel(PCSel));
  Register #(.width(32)) register_1 (.D(multiplexer_2_out), .clk(clk), .Q(Instruction_t));  // open: en, clr
  Multiplexer #(.width(32)) multiplexer_2 (.in0(Instruction), .in1(32'h13), .out(multiplexer_2_out), .sel(PCSel));
  Multiplexer #(.select(2), .width(32)) multiplexer_3 (
    .in0(MemDataToReg), .in1(MemAddress), .in2(ProgramCounter), .out(RegWriteData), .sel(WBSEl));  // open: in3
  Adder #(.width(32)) adder_1 (.a(ProgramCounter), .b(32'h4), .out(PCInc));  // open: cin, cout
  control_logic control_logic_1 (
    .PCSel(PCSel), .RegWEn(RegWEn), .ImmSel(ImmSel), .BrUn(BrUn), .ASel(ASel), .BSel(BSel), .ALUSel(ALUSel),
    .MemWEn(MemWEn), .WBSel(WBSEl), .Instruction(Instruction_t), .BrEq(BrEq), .BrLt(BrLt));
  regfile regfile_1 (
    .ReadReg1(Instruction_t[19:15]), .ReadReg2(Instruction_t[24:20]), .WriteReg(Instruction_t[11:7]),
    .RegWriteData(RegWriteData), .RegWEn(RegWEn), .clk(clk), .ra(ra), .sp(sp), .t0(t0), .t1(t1), .t2(t2),
    .s0(s0), .s1(s1), .a0(a0), .RegReadData1(RegReadData1), .RegReadData2(RegReadData2));
  imm_gen imm_gen_1 (.Instruction(Instruction_t), .ImmSel(ImmSel), .Immediate(Immediate));
  Adder #(.width(32)) adder_2 (.a(ProgramCounter), .b(32'hfffffffc), .out(adder_2_out));  // open: cin, cout
  Multiplexer #(.width(32)) multiplexer_4 (.in0(adder_2_out), .in1(RegReadData1), .out(multiplexer_4_out), .sel(ASel));
  Multiplexer #(.width(32)) multiplexer_5 (.in0(Immediate), .in1(RegReadData2), .out(multiplexer_5_out), .sel(BSel));
  alu alu_1 (.ALUResult(MemAddress), .A(multiplexer_4_out), .B(multiplexer_5_out), .ALUSel(ALUSel));
  branch_comp branch_comp_1 (.BrData1(RegReadData1), .BrData2(RegReadData2), .BrUn(BrUn), .BrEq(BrEq), .BrLt(BrLt));
  partial_store partial_store_1 (
    .Instruction(Instruction_t), .MemAddress(MemAddress), .DataFromReg(RegReadData2), .MemWEn(MemWEn),
    .MemWriteMask(MemWriteMask), .DataToMem(MemWriteData));
  partial_load partial_load_1 (
    .Instruction(Instruction_t), .MemAddress(MemAddress), .DataFromMem(MemReadData), .DataToReg(MemDataToReg));

  // Other names for the same wires on the sheet: ALUResult[31:0] = MemAddress; FetchInstruction[31:0] = Instruction;
  //   WriteReg[4:0] = Instruction_t[11:7]; ReadReg1[4:0] = Instruction_t[19:15]; ReadReg2[4:0] = Instruction_t[24:20]

  // Notes on the sheet:
  //   To IMEM
  //   IMEM (do **NOT** move this)
  //   From IMEM
  //   Inputs/Outputs for testing. Do **NOT** move these.
  //   It is OK to move the PC, RegFile, ALU, MEM, Branch Comp, Imm Gen, Partial Load, Partial Store and Control Logic to wherever is most convenient for you when constructing your CPU, and to delete this text
  //   To DMEM
  //   DMEM (do **NOT** move this)
  //   From DMEM
endmodule
