// Logisim project imm-gen.circ as structural Verilog: 1 circuit, main circuit imm_gen
module imm_gen (
  input  [31:0] Instruction,
  input  [2:0] ImmSel,
  output [31:0] Immediate
);

  wire [31:0] B_Immediate, I_Immediate, J_Immediate, S_Immediate, U_Immediate;

  Multiplexer #(.select(3), .width(32)) multiplexer_1 (
    .in0(I_Immediate), .in1(S_Immediate), .in2(B_Immediate), .in3(U_Immediate), .in4(J_Immediate),
    .out(Immediate), .sel(ImmSel));  // open: in5, in6, in7
  assign I_Immediate = {{20{Instruction[31]}}, Instruction[31:20]};  // Bit_Extender bit_extender_1
  assign S_Immediate = {{20{Instruction[31]}}, {Instruction[31:25], Instruction[11:7]}};  // Bit_Extender bit_extender_2
  assign B_Immediate = {{19{Instruction[31]}}, {Instruction[31], Instruction[7], Instruction[30:25], Instruction[11:8], 1'b0}};  // Bit_Extender bit_extender_3
  assign U_Immediate = Instruction & 32'hfffff000;  // AND_Gate and_1, 32 bits wide
  assign J_Immediate = {{11{Instruction[31]}}, {Instruction[31], Instruction[19:12], Instruction[20], Instruction[30:21], 1'b0}};  // Bit_Extender bit_extender_4

  // Notes on the sheet:
  //   INPUTS to your circuit
  //   DON'T CHANGE THE LOCATIONS OF THE INPUTS AND OUTPUTS!
  //   OUTPUT from your circuit
endmodule
