// Logisim project partial-load.circ as structural Verilog: 1 circuit, main circuit partial_load
module partial_load (
  input  [31:0] Instruction,
  input  [31:0] MemAddress,
  input  [31:0] DataFromMem,
  output [31:0] DataToReg
);

  wire [31:0] lbData, lhData, shifter_1_out;

  Shifter #(.shift("lr"), .width(32)) shifter_1 (
    .in(DataFromMem), .\dist ({MemAddress[1:0], 3'b000}), .out(shifter_1_out));
  Multiplexer #(.select(2), .width(32)) multiplexer_1 (
    .in0(lbData), .in1(lhData), .in2(DataFromMem), .out(DataToReg), .sel(Instruction[13:12]));  // open: in3
  assign lbData = {{24{shifter_1_out[7]}}, shifter_1_out[7:0]};  // Bit_Extender bit_extender_1
  assign lhData = {{16{shifter_1_out[15]}}, shifter_1_out[15:0]};  // Bit_Extender bit_extender_2

  // Other names for the same wires on the sheet: funct3[1:0] = Instruction[13:12]; lowmem[1:0] = MemAddress[1:0]

  // Notes on the sheet:
  //   INPUTS to your circuit
  //   DON'T CHANGE THE LOCATIONS OF THE INPUTS AND OUTPUTS!
  //   OUTPUT from your circuit
endmodule
