// Logisim project partial-store.circ as structural Verilog: 1 circuit, main circuit partial_store
module partial_store (
  input  [31:0] Instruction,
  input  [31:0] MemAddress,
  input  [31:0] DataFromReg,
  input  MemWEn,
  output [3:0] MemWriteMask,
  output [31:0] DataToMem
);

  wire [3:0] multiplexer_1_out, shifter_2_out;

  Multiplexer #(.select(2), .width(4)) multiplexer_1 (
    .in0(4'b0001), .in1(4'b0011), .in2(4'b1111), .out(multiplexer_1_out), .sel(Instruction[13:12]));  // open: in3
  Shifter #(.width(32)) shifter_1 (.in(DataFromReg), .\dist ({MemAddress[1:0], 3'b000}), .out(DataToMem));
  Shifter #(.width(4)) shifter_2 (.in(multiplexer_1_out), .\dist (MemAddress[1:0]), .out(shifter_2_out));
  Multiplexer #(.width(4)) multiplexer_2 (.in0(4'b0000), .in1(shifter_2_out), .out(MemWriteMask), .sel(MemWEn));

  // Other names for the same wires on the sheet: funct3[1:0] = Instruction[13:12]; lowMem[1:0] = MemAddress[1:0]

  // Notes on the sheet:
  //   INPUTS to your circuit
  //   DON'T CHANGE THE LOCATIONS OF THE INPUTS AND OUTPUTS!
  //   OUTPUT from your circuit
endmodule
