// Logisim project regfile.circ as structural Verilog: 1 circuit, main circuit regfile
module regfile (
  input  [4:0] ReadReg1,
  input  [4:0] ReadReg2,
  input  [4:0] WriteReg,
  input  [31:0] RegWriteData,
  input  RegWEn,
  input  clk,
  output [31:0] ra,
  output [31:0] sp,
  output [31:0] t0,
  output [31:0] t1,
  output [31:0] t2,
  output [31:0] s0,
  output [31:0] s1,
  output [31:0] a0,
  output [31:0] RegReadData1,
  output [31:0] RegReadData2
);

  wire and_1_out, x1w, x2w, x3w, x4w, x5w, x6w, x7w, x8w, x9w, x10w, x11w, x12w, x13w, x14w, x15w, x16w,
       x17w, x18w, x19w, x20w, x21w, x22w, x23w, x24w, x25w, x26w, x27w, x28w, x29w, x30w, x31w;
  wire [31:0] x3, x4, x11, x12, x13, x14, x15, x16, x17, x18, x19, x20, x21, x22, x23, x24, x25, x26, x27,
       x28, x29, x30, x31;

  Register #(.width(32)) register_1 (.D(RegWriteData), .en(x1w), .clk(and_1_out), .Q(ra));  // open: clr
  Register #(.width(32)) register_2 (.D(RegWriteData), .en(x17w), .clk(and_1_out), .Q(x17));  // open: clr
  and and_1 (and_1_out, RegWEn, clk);
  Demultiplexer #(.select(5)) demultiplexer_1 (
    .out1(x1w), .out2(x2w), .out3(x3w), .out4(x4w), .out5(x5w), .out6(x6w), .out7(x7w), .out8(x8w),
    .out9(x9w), .out10(x10w), .out11(x11w), .out12(x12w), .out13(x13w), .out14(x14w), .out15(x15w),
    .out16(x16w), .out17(x17w), .out18(x18w), .out19(x19w), .out20(x20w), .out21(x21w), .out22(x22w),
    .out23(x23w), .out24(x24w), .out25(x25w), .out26(x26w), .out27(x27w), .out28(x28w), .out29(x29w),
    .out30(x30w), .out31(x31w), .in(1'b1), .sel(WriteReg));  // open: out0
  Register #(.width(32)) register_3 (.D(RegWriteData), .en(x2w), .clk(and_1_out), .Q(sp));  // open: clr
  Register #(.width(32)) register_4 (.D(RegWriteData), .en(x18w), .clk(and_1_out), .Q(x18));  // open: clr
  Register #(.width(32)) register_5 (.D(RegWriteData), .en(x3w), .clk(and_1_out), .Q(x3));  // open: clr
  Register #(.width(32)) register_6 (.D(RegWriteData), .en(x19w), .clk(and_1_out), .Q(x19));  // open: clr
  Register #(.width(32)) register_7 (.D(RegWriteData), .en(x4w), .clk(and_1_out), .Q(x4));  // open: clr
  Register #(.width(32)) register_8 (.D(RegWriteData), .en(x20w), .clk(and_1_out), .Q(x20));  // open: clr
  Register #(.width(32)) register_9 (.D(RegWriteData), .en(x5w), .clk(and_1_out), .Q(t0));  // open: clr
  Register #(.width(32)) register_10 (.D(RegWriteData), .en(x21w), .clk(and_1_out), .Q(x21));  // open: clr
  Multiplexer #(.select(5), .width(32)) multiplexer_1 (
    .in0({32{1'b0}}), .in1(ra), .in2(sp), .in3(x3), .in4(x4), .in5(t0), .in6(t1), .in7(t2), .in8(s0),
    .in9(s1), .in10(a0), .in11(x11), .in12(x12), .in13(x13), .in14(x14), .in15(x15), .in16(x16), .in17(x17),
    .in18(x18), .in19(x19), .in20(x20), .in21(x21), .in22(x22), .in23(x23), .in24(x24), .in25(x25),
    .in26(x26), .in27(x27), .in28(x28), .in29(x29), .in30(x30), .in31(x31), .out(RegReadData1), .sel(ReadReg1));
  Register #(.width(32)) register_11 (.D(RegWriteData), .en(x6w), .clk(and_1_out), .Q(t1));  // open: clr
  Register #(.width(32)) register_12 (.D(RegWriteData), .en(x22w), .clk(and_1_out), .Q(x22));  // open: clr
  Register #(.width(32)) register_13 (.D(RegWriteData), .en(x7w), .clk(and_1_out), .Q(t2));  // open: clr
  Register #(.width(32)) register_14 (.D(RegWriteData), .en(x23w), .clk(and_1_out), .Q(x23));  // open: clr
  Register #(.width(32)) register_15 (.D(RegWriteData), .en(x8w), .clk(and_1_out), .Q(s0));  // open: clr
  Register #(.width(32)) register_16 (.D(RegWriteData), .en(x24w), .clk(and_1_out), .Q(x24));  // open: clr
  Multiplexer #(.select(5), .width(32)) multiplexer_2 (
    .in0({32{1'b0}}), .in1(ra), .in2(sp), .in3(x3), .in4(x4), .in5(t0), .in6(t1), .in7(t2), .in8(s0),
    .in9(s1), .in10(a0), .in11(x11), .in12(x12), .in13(x13), .in14(x14), .in15(x15), .in16(x16), .in17(x17),
    .in18(x18), .in19(x19), .in20(x20), .in21(x21), .in22(x22), .in23(x23), .in24(x24), .in25(x25),
    .in26(x26), .in27(x27), .in28(x28), .in29(x29), .in30(x30), .in31(x31), .out(RegReadData2), .sel(ReadReg2));
  Register #(.width(32)) register_17 (.D(RegWriteData), .en(x9w), .clk(and_1_out), .Q(s1));  // open: clr
  Register #(.width(32)) register_18 (.D(RegWriteData), .en(x25w), .clk(and_1_out), .Q(x25));  // open: clr
  Register #(.width(32)) register_19 (.D(RegWriteData), .en(x10w), .clk(and_1_out), .Q(a0));  // open: clr
  Register #(.width(32)) register_20 (.D(RegWriteData), .en(x26w), .clk(and_1_out), .Q(x26));  // open: clr
  Register #(.width(32)) register_21 (.D(RegWriteData), .en(x11w), .clk(and_1_out), .Q(x11));  // open: clr
  Register #(.width(32)) register_22 (.D(RegWriteData), .en(x27w), .clk(and_1_out), .Q(x27));  // open: clr
  Register #(.width(32)) register_23 (.D(RegWriteData), .en(x12w), .clk(and_1_out), .Q(x12));  // open: clr
  Register #(.width(32)) register_24 (.D(RegWriteData), .en(x28w), .clk(and_1_out), .Q(x28));  // open: clr
  Register #(.width(32)) register_25 (.D(RegWriteData), .en(x13w), .clk(and_1_out), .Q(x13));  // open: clr
  Register #(.width(32)) register_26 (.D(RegWriteData), .en(x29w), .clk(and_1_out), .Q(x29));  // open: clr
  Register #(.width(32)) register_27 (.D(RegWriteData), .en(x14w), .clk(and_1_out), .Q(x14));  // open: clr
  Register #(.width(32)) register_28 (.D(RegWriteData), .en(x30w), .clk(and_1_out), .Q(x30));  // open: clr
  Register #(.width(32)) register_29 (.D(RegWriteData), .en(x15w), .clk(and_1_out), .Q(x15));  // open: clr
  Register #(.width(32)) register_30 (.D(RegWriteData), .en(x31w), .clk(and_1_out), .Q(x31));  // open: clr
  Register #(.width(32)) register_31 (.D(RegWriteData), .en(x16w), .clk(and_1_out), .Q(x16));  // open: clr

  // Other names for the same wires on the sheet: x1[31:0] = ra; x2[31:0] = sp; x5[31:0] = t0; x6[31:0] = t1;
  //   x7[31:0] = t2; x8[31:0] = s0; x9[31:0] = s1; x10[31:0] = a0

  // Notes on the sheet:
  //   INPUTS to your circuit
  //   DON'T CHANGE THE LOCATIONS OF THE INPUTS AND OUTPUTS!
  //   These are DEBUG/TEST outputs from your circuit.
  //   OUTPUTS from your circuit
endmodule
